# Fritzing sketch CentralAlarm (saved by Fritzing 0.9.4)
breadboards: 1

parts:
  U1 = NodeMCU V1.0
  Componente1 = LCD1602-I2C
  Part1 = KY-006 Passive Buzzer Module [package="Breakout board"]
  R1 = Resistor [tolerance=±5% resistance=220 package=THT]
  RE1 = KY-040 Rotary encoder [package=THT]
  LED1 = RGB LED - (4 legs) [package="5 mm [THT]"]

nets:
  N1: U1.D0, LED1.red_cathode
  N2: U1.D1, Componente1.SCL
  N3: U1.D2, Componente1.SDA
  N4: U1.D3, RE1.CLK
  N5: U1.D4, RE1.DT
  3V3: U1.3V3, R1.Pin_0, RE1.Vcc, LED1.blue_cathode
  GND: U1.GND, Componente1.GND, RE1.GND
  N6: U1.D5, RE1.SW
  N7: U1.D6, Part1.-
  N8: U1.D7, LED1.green_cathode
  N9: U1.D8, LED1.common_anode
  VIN: U1.Vin, Componente1.VCC
  N10: Part1.S, R1.Pin_1

custom parts:
  NodeMCU V1.0: ESP8266 based NodeMCU
  LCD1602-I2C: A standard character display, usually with 2x16 characters. Comes in many colors with LCM1602 IIC attached.
  KY-006 Passive Buzzer Module: Passive Piezoelectric Buzzer Module Keyes KY-006, it can produce a range of sound tones depending on the input frequency.
  KY-040 Rotary encoder: KY-040 Rotary Encoder with switch on breakout borad from AZ Delivery
