# Fritzing sketch FireNode (saved by Fritzing 0.9.4)
breadboards: 1

parts:
  U1 = NodeMCU V1.0
  Mod1 = KY-026 Flame Sensor Module [package="Breakout board"]

nets:
  N1: U1.D1, Mod1.D0
  N2: U1.GND, Mod1.G
  N3: U1.Vin, Mod1.+
  N4: U1.A0, Mod1.A0

custom parts:
  NodeMCU V1.0: ESP8266 based NodeMCU
  KY-026 Flame Sensor Module: KY-026 Flame Sensor Module reacts in the presence of fire.
