# Fritzing sketch TecaNode (saved by Fritzing 0.9.4)
breadboards: 1

parts:
  U1 = NodeMCU V1.0
  HC-SR04_Sensor_1 = HC-SR04 Ultrasonic Distance Sensor
  Mod1 = KY-018 Photoresistor Module [package="Breakout board"]
  DHT1 = DHT11 Humitidy and Temperature Sensor
  Mod2 = KY-031 Knock Sensor Module [package="Breakout board"]
  R2 = Resistor [tolerance=±5% resistance=22k package=THT]
  R3 = Resistor [tolerance=±5% resistance=10 package=THT]

nets:
  N1: U1.D0, HC-SR04_Sensor_1.TRIG
  3V3: U1.3V3, Mod1.-, DHT1.NULL, Mod2.Vin
  GND: U1.GND, HC-SR04_Sensor_1.GND, Mod1.Vin, DHT1.GND, Mod2.-, R2.Pin_0
  N2: U1.D5, DHT1.VDD
  N3: U1.D6, Mod2.S
  N4: U1.D7, R3.Pin_1
  VIN: U1.Vin, HC-SR04_Sensor_1.VCC
  N5: U1.A0, Mod1.S
  N6: HC-SR04_Sensor_1.ECHO, R2.Pin_1, R3.Pin_0

custom parts:
  NodeMCU V1.0: ESP8266 based NodeMCU
  KY-018 Photoresistor Module: KY-018 Photoresistor module, used to measure light intensity. It can determine the presence or absence of light.
  DHT11 Humitidy and Temperature Sensor: DHT11 Humidity and Temperature Sensor
  KY-031 Knock Sensor Module: KY-031 Knock Sensor module. A vibration sensor that sends a signal when a knock/tap is detected.
